// Logisim project lab1.circ as structural Verilog: 1 circuit, main circuit main
module main (
);

  wire T_Flip_Flop_q;
  wire [2:0] Current_State_q;
  wire [5:0] rom_1_data;

  // Probe on rom_1_data[2:0]
  Register #(.width(3), .trigger("falling")) Current_State (
    .D(rom_1_data[2:0]), .Q(Current_State_q), .clk(T_Flip_Flop_q));  // open: en, clr
  T_Flip_Flop T_Flip_Flop (.Q(T_Flip_Flop_q));  // open: clk, T, Qn, preset, reset, en
  // Probe on Current_State_q
  ROM #(.addrWidth(3), .dataWidth(6)) rom_1 (.addr(Current_State_q), .data(rom_1_data));  // open: sel
  // Probe on rom_1_data
  LED o2 (.in(rom_1_data[5]));
  LED o1 (.in(rom_1_data[4]));
  LED o0 (.in(rom_1_data[3]));

  // Notes on the sheet:
  //   ROM
  //   contents of rom_1 (hex, n*v repeats v):
  //   23 1c 0 35 a 3f 6 39
endmodule
