// Logisim project Lab Support.circ as structural Verilog: 2 circuits, main circuit ALU
module ALU (
  input  [31:0] X_32,
  input  [31:0] Y_32,
  input  [3:0] Opr_4,
  output [31:0] R_32,
  output Z,
  output N,
  output C,
  output V
);

  wire ADD, ADD_or_SUB, adder_1_cout, AND, and_2_out, and_3_out, and_4_out, and_5_out, LSR, LSR_Carry,
       multiplexer_2_out, NOP, NotY, OR, or_1_out, or_4_out, RY, SUB, xnor_1_out, XOR, xor_2_out, xor_3_out,
       xor_4_out;
  wire [31:0] adder_1_out, and_1_out, multiplexer_1_out, multiplexer_3_out, not_1_out, or_3_out,
       shifter_1_out, xor_1_out;

  Decoder #(.select(4)) decoder_1 (
    .out0(NOP), .out1(ADD), .out2(SUB), .out3(RY), .out4(AND), .out5(OR), .out6(XOR), .out7(NotY),
    .out8(LSR), .sel(Opr_4));  // open: out9, out10, out11, out12, out13, out14, out15, en
  assign xor_1_out = X_32 ^ Y_32;  // XOR_Gate xor_1, 32 bits wide
  assign not_1_out = ~Y_32;  // NOT_Gate not_1, 32 bits wide
  assign {N, R_32[30:0]} = NotY ? not_1_out : 32'bz;  // Controlled_Buffer controlled_buffer_1
  assign {N, R_32[30:0]} = or_1_out ? Y_32 : 32'bz;  // Controlled_Buffer controlled_buffer_2
  or or_1 (or_1_out, NOP, RY);
  or or_2 (ADD_or_SUB, ADD, SUB);
  assign {N, R_32[30:0]} = XOR ? xor_1_out : 32'bz;  // Controlled_Buffer controlled_buffer_3
  // Probe on X_32
  Multiplexer #(.width(32)) multiplexer_1 (
    .in0(Y_32), .in1(not_1_out), .out(multiplexer_1_out), .sel(SUB));  // open: en
  // Probe on multiplexer_1_out
  Adder #(.width(32)) adder_1 (.a(X_32), .b(multiplexer_1_out), .out(adder_1_out), .cin(SUB), .cout(adder_1_cout));
  xor xor_2 (xor_2_out, N, X_32[31]);
  xnor xnor_1 (xnor_1_out, X_32[31], Y_32[31]);
  xor xor_3 (xor_3_out, N, X_32[31]);
  xor xor_4 (xor_4_out, X_32[31], Y_32[31]);
  assign or_3_out = X_32 | Y_32;  // OR_Gate or_3, 32 bits wide
  assign {N, R_32[30:0]} = AND ? and_1_out : 32'bz;  // Controlled_Buffer controlled_buffer_4
  assign and_1_out = X_32 & Y_32;  // AND_Gate and_1, 32 bits wide
  assign {N, R_32[30:0]} = ADD_or_SUB ? adder_1_out : 32'bz;  // Controlled_Buffer controlled_buffer_5
  and and_2 (and_2_out, xor_2_out, xnor_1_out, ADD);
  and and_3 (and_3_out, xor_3_out, xor_4_out, SUB);
  assign {N, R_32[30:0]} = OR ? or_3_out : 32'bz;  // Controlled_Buffer controlled_buffer_6
  Shifter #(.width(32), .shift("lr")) shifter_1 (.in(X_32), .\dist (Y_32[4:0]), .out(shifter_1_out));
  Multiplexer #(.select(5)) multiplexer_2 (
    .in0(1'b0), .in1(X_32[0]), .in2(X_32[1]), .in3(X_32[2]), .in4(X_32[3]), .in5(X_32[4]), .in6(X_32[5]),
    .in7(X_32[6]), .in8(X_32[7]), .in9(X_32[8]), .in10(X_32[9]), .in11(X_32[10]), .in12(X_32[11]),
    .in13(X_32[12]), .in14(X_32[13]), .in15(X_32[14]), .in16(X_32[15]), .in17(X_32[16]), .in18(X_32[17]),
    .in19(X_32[18]), .in20(X_32[19]), .in21(X_32[20]), .in22(X_32[21]), .in23(X_32[22]), .in24(X_32[23]),
    .in25(X_32[24]), .in26(X_32[25]), .in27(X_32[26]), .in28(X_32[27]), .in29(X_32[28]), .in30(X_32[29]),
    .in31(X_32[30]), .out(multiplexer_2_out), .sel(Y_32[4:0]));  // open: en
  and and_4 (and_4_out, X_32[31], Y_32[5]);
  and and_5 (and_5_out, adder_1_cout, ADD_or_SUB);
  or or_4 (or_4_out, multiplexer_2_out, and_4_out);
  or or_5 (V, and_2_out, and_3_out);
  assign {N, R_32[30:0]} = LSR ? multiplexer_3_out : 32'bz;  // Controlled_Buffer controlled_buffer_7
  Multiplexer #(.width(32)) multiplexer_3 (
    .in0(shifter_1_out), .in1({32{1'b0}}), .out(multiplexer_3_out), .sel(Y_32[5]));  // open: en
  and and_6 (LSR_Carry, or_4_out, LSR);
  or or_6 (C, and_5_out, LSR_Carry);
  nor nor_1 (Z, R_32[0], R_32[1], R_32[2], R_32[3], R_32[4], R_32[5], R_32[6], R_32[7], R_32[8], R_32[9], R_32[10], R_32[11], R_32[12], R_32[13], R_32[14], R_32[15], R_32[16], R_32[17], R_32[18], R_32[19], R_32[20], R_32[21], R_32[22], R_32[23], R_32[24], R_32[25], R_32[26], R_32[27], R_32[28], R_32[29], R_32[30], N);

  assign R_32[31] = N;

  // Other names for the same wires on the sheet: R[31:0] = {N, R_32[30:0]}; msb_R = N; X[31:0] = X_32;
  //   msb_X = X_32[31]; LSRcount5[4:0] = Y_32[4:0]; Y[31:0] = Y_32; LSRcount6 = Y_32[5]; msb_Y = Y_32[31]

  // Notes on the sheet:
  //   Logical Shift Right = 1000
  //   NOP = 0000
  //   ADD = 0001
  //   SUB = 0010
  //   RY = 0011
  //   AND = 0100
  //   OR = 0101
  //   XOR = 0110
  //   NotY = 0111
  //   Operation Decoder
  //   "don't care" for NOP
  //   so do RY ... simple
  //   added Sept/2015
  //   NOT Y
  //   oVerflow detector
  //   X
  //   Y
  //   Only C = 1  if ADD or SUB
  //   Only V = 1 this way  if ADD
  //   Only V = 1 this way  if SUB
  //   if F==0 do not update FLAGS
  //   F pin REMOVED!   Sept/2015
  //   Clock REMOVED! Sept/2015
  //   zero detector
  //   Flip Flops REMOVED! Sept/2015
  //   Clear input REMOVED! Sept/2015
endmodule

module Reg32 (
  input  [31:0] DIn_32,
  input  CE,
  input  CLK,
  input  OE,
  input  Clear,
  output [31:0] Debug_Q_32,
  output [31:0] DOut_32
);

  Register #(.width(32), .trigger("falling")) Logisim_Register (
    .D(DIn_32), .en(CE), .Q(Debug_Q_32), .clk(CLK), .clr(Clear));
  assign DOut_32 = OE ? Debug_Q_32 : 32'bz;  // Controlled_Buffer controlled_buffer_1
endmodule
