// Logisim project Lab-II_Part1.circ as structural Verilog: 1 circuit, main circuit main
module main (
);

  wire Clk, Clr, not_1_out, or_1_out, T1CE, T1OE, T2CE, T2OE, WordR, WordW;
  wire [1:0] register_1_q, rom_1_data;
  wire [3:0] OPR, Reg;
  wire [31:0] alu_1_r_32, DATA, reg32_1_debug_q_32, reg32_1_dout_32, reg32_2_debug_q_32;

  // Probe on rom_1_data
  Register #(.width(2)) register_1 (.D(rom_1_data), .Q(register_1_q), .clk(Clk));  // open: en, clr
  // Probe on reg32_1_debug_q_32
  Reg32 reg32_1 (
    .DIn_32(DATA), .CE(T1CE), .DOut_32(reg32_1_dout_32), .Debug_Q_32(reg32_1_debug_q_32), .CLK(Clk), .OE(T1OE));  // open: Clear
  // Probe on register_1_q
  ROM #(.addrWidth(2), .dataWidth(16)) rom_1 (
    .addr(register_1_q), .data({OPR, Reg, WordR, WordW, T1CE, T1OE, T2CE, T2OE, rom_1_data}));  // open: sel
  ALU alu_1 (.X_32(reg32_1_dout_32), .Y_32(DATA), .Opr_4(OPR), .R_32(alu_1_r_32));  // open: C, V, N, Z
  // Probe on {OPR, Reg, WordR, WordW, T1CE, T1OE, T2CE, T2OE, rom_1_data}
  // Probe on reg32_2_debug_q_32
  Reg32 reg32_2 (
    .DIn_32(alu_1_r_32), .CE(T2CE), .DOut_32(DATA), .Debug_Q_32(reg32_2_debug_q_32), .CLK(Clk), .OE(T2OE));  // open: Clear
  // Probe on OPR
  T_Flip_Flop Toggle_Switch (.Q(Clk));  // open: clk, T, Qn, preset, reset, en
  Button button_1 (.out(Clr));
  // Probe on WordR
  // Probe on Reg
  or or_1 (or_1_out, WordR, WordW);
  // Probe on T1CE
  // Probe on WordW
  not not_1 (not_1_out, Clk);
  // Probe on T1OE
  // Probe on T2CE
  RAM #(.addrWidth(4), .dataWidth(32)) ram_1 (
    .addr(Reg), .data(DATA), .sel(or_1_out), .clk(not_1_out), .ld(WordR), .clr(Clr));
  // Probe on T2OE

  // Notes on the sheet:
  //   "1. ROM-Based FSM Circuit"
  //   "2. ALU Circuit"
  //   contents of rom_1 (hex, n*v repeats v):
  //   a1 1c9a d44
  //   "3. RAM Circuit"
endmodule
