// Logisim project Lab-II_Part2.circ as structural Verilog: 1 circuit, main circuit main
module main (
);

  wire and_1_out, ANOP, AOP, Clk, Clr, DR, not_1_out, or_1_out, src, SXR, SYR, T1CE, T1OE, T2CE, T2OE, WordR,
       WordW;
  wire [1:0] multiplexer_1_out, register_1_q, rom_1_data;
  wire [3:0] OPR, Reg;
  wire [15:0] IR_q;
  wire [31:0] alu_1_r_32, DATA, reg32_1_debug_q_32, reg32_1_dout_32, reg32_2_debug_q_32;

  // Probe on 2'b10
  Multiplexer #(.width(2), .enable("false")) multiplexer_1 (
    .in0(rom_1_data), .in1(2'b10), .out(multiplexer_1_out), .sel(and_1_out));
  // Probe on reg32_1_debug_q_32
  Reg32 reg32_1 (
    .DIn_32(DATA), .CE(T1CE), .DOut_32(reg32_1_dout_32), .Debug_Q_32(reg32_1_debug_q_32), .CLK(Clk), .OE(T1OE));  // open: Clear
  and and_1 (and_1_out, ~register_1_q[0], ~register_1_q[1], src);  // AND_Gate
  // Probe on register_1_q
  Register #(.width(2)) register_1 (.D(multiplexer_1_out), .Q(register_1_q), .clk(Clk));  // open: en, clr
  ALU alu_1 (.X_32(reg32_1_dout_32), .Y_32(DATA), .Opr_4(OPR), .R_32(alu_1_r_32));  // open: C, V, N, Z
  ROM #(.addrWidth(2), .dataWidth(13)) rom_1 (
    .addr(register_1_q), .data({AOP, ANOP, DR, SXR, SYR, WordR, WordW, T1CE, T1OE, T2CE, T2OE, rom_1_data}));  // open: sel
  // Probe on {AOP, ANOP, DR, SXR, SYR, WordR, WordW, T1CE, T1OE, T2CE, T2OE, rom_1_data}
  // Probe on reg32_2_debug_q_32
  Reg32 reg32_2 (
    .DIn_32(alu_1_r_32), .CE(T2CE), .DOut_32(DATA), .Debug_Q_32(reg32_2_debug_q_32), .CLK(Clk), .OE(T2OE));  // open: Clear
  T_Flip_Flop Toggle_Switch (.Q(Clk));  // open: clk, T, Qn, preset, reset, en
  Button button_1 (.out(Clr));
  assign OPR = ANOP ? 4'b0000 : 4'bz;  // Controlled_Buffer controlled_buffer_1
  // Probe on OPR
  Register #(.width(16)) IR (.Q(IR_q));  // open: D, en, clk, clr
  // Probe on OPR
  // Probe on Reg
  // Probe on Reg
  // Probe on WordR
  // Probe on WordW
  or or_1 (or_1_out, WordR, WordW);
  // Probe on T1CE
  // Probe on T1OE
  assign Reg = SYR ? IR_q[3:0] : 4'bz;  // Controlled_Buffer controlled_buffer_2
  assign Reg = SXR ? IR_q[7:4] : 4'bz;  // Controlled_Buffer controlled_buffer_3
  assign Reg = DR ? IR_q[11:8] : 4'bz;  // Controlled_Buffer controlled_buffer_4
  assign OPR = AOP ? IR_q[15:12] : 4'bz;  // Controlled_Buffer controlled_buffer_5
  not not_1 (not_1_out, Clk);
  // Probe on T2CE
  // Probe on T2OE
  and and_2 (src, IR_q[12], IR_q[13], ~IR_q[15]);  // AND_Gate
  RAM #(.addrWidth(4), .dataWidth(32)) ram_1 (
    .addr(Reg), .data(DATA), .sel(or_1_out), .clk(not_1_out), .ld(WordR), .clr(Clr));

  // Notes on the sheet:
  //   "2. ALU Circuit"
  //   contents of rom_1 (hex, n*v repeats v):
  //   801 aa2 119b c44
  //   "1. ROM-Based FSM Circuit"
  //   "3. RAM Circuit"
endmodule
