// Logisim project Lab3Part2.circ as structural Verilog: 1 circuit, main circuit main
module main (
);

  wire AADD, alu_1_c, alu_1_n, alu_1_v, alu_1_z, and_1_out, and_2_out, ANOP, AOP, C1OE, Clock, CLR, DR,
       IBRead, IBWrite, Inverted_Clock, IRCE, MARCE, MAROE, MDRCE, MDRget, MDROE, MDRput, nor_1_out,
       not_1_out, or_1_out, PCOE, RegLD, RegSEL, SXR, SYR, T1CE, T1OE, T2CE, T2OE;
  wire [3:0] Opr, RegisterAddressBus;
  wire [7:0] Current_State_q, multiplexer_1_out, NextState, opcode, rom_1_data;
  wire [23:0] Instruction_Register_q;
  wire [31:0] alu_1_r_32, controlled_buffer_9_out, InterconnectionAddressBus, InterconnectionDataBus,
       InternalDataBus, reg32_1_debug_q_32, reg32_1_dout_32, reg32_2_debug_q_32, reg32_3_debug_q_32,
       reg32_3_dout_32, reg32_4_debug_q_32;
  wire [31:31] rom_2_data;

  // Probe on opcode
  Button Press_to_Clear_Internal_Processor_State (.out(CLR));
  not not_1 (not_1_out, Clock);
  and and_1 (and_1_out, Current_State_q[0], Current_State_q[1], ~Current_State_q[2], ~Current_State_q[3], ~Current_State_q[4], ~Current_State_q[5], ~Current_State_q[6], ~Current_State_q[7]);  // AND_Gate
  // Probe on reg32_1_debug_q_32
  Reg32 reg32_1 (
    .DIn_32(InternalDataBus), .CE(T1CE), .DOut_32(reg32_1_dout_32), .Debug_Q_32(reg32_1_debug_q_32),
    .CLK(Clock), .OE(T1OE), .Clear(CLR));
  Register #(.width(32)) Instruction_Register (
    .D(InternalDataBus), .en(IRCE), .Q({opcode, Instruction_Register_q}), .clk(not_1_out));  // open: clr
  ROM rom_1 (.addr(opcode), .data(rom_1_data), .sel(and_1_out));
  Multiplexer #(.width(8), .enable("false")) multiplexer_1 (
    .in0(NextState), .in1(rom_1_data), .out(multiplexer_1_out), .sel(and_1_out));
  // Probe on multiplexer_1_out
  // Probe on reg32_1_dout_32
  assign RegisterAddressBus = SYR ? Instruction_Register_q[15:12] : 4'bz;  // Controlled_Buffer controlled_buffer_1
  Register Current_State (.D(multiplexer_1_out), .Q(Current_State_q), .clk(Clock), .clr(CLR));  // open: en
  // Probe on InternalDataBus
  assign RegisterAddressBus = SXR ? Instruction_Register_q[19:16] : 4'bz;  // Controlled_Buffer controlled_buffer_2
  // Probe on alu_1_r_32
  ALU alu_1 (
    .X_32(reg32_1_dout_32), .Y_32(InternalDataBus), .Opr_4(Opr), .R_32(alu_1_r_32), .C(alu_1_c), .V(alu_1_v),
    .N(alu_1_n), .Z(alu_1_z));
  LED led_1 (.in(alu_1_c));
  LED led_2 (.in(alu_1_v));
  LED led_3 (.in(alu_1_n));
  LED led_4 (.in(alu_1_z));
  Clock Testing_clock (.out(Clock));
  assign RegisterAddressBus = DR ? Instruction_Register_q[23:20] : 4'bz;  // Controlled_Buffer controlled_buffer_3
  assign Opr = AOP ? opcode[3:0] : 4'bz;  // Controlled_Buffer controlled_buffer_4
  assign Opr = ANOP ? 4'b0000 : 4'bz;  // Controlled_Buffer controlled_buffer_5
  ROM #(.dataWidth(32)) rom_2 (
    .addr(Current_State_q),
    .data({rom_2_data[31], IRCE, PCOE, C1OE, AADD, MARCE, MAROE, MDRCE, MDROE, MDRget, MDRput, IBRead, IBWrite, AOP, ANOP, DR, SXR, SYR, RegSEL, RegLD, T1CE, T1OE, T2CE, T2OE, NextState}));  // open: sel
  // Probe on reg32_2_debug_q_32
  not not_2 (Inverted_Clock, Clock);
  // Probe on NextState
  Reg32 reg32_2 (
    .DIn_32(alu_1_r_32), .CE(T2CE), .DOut_32(InternalDataBus), .Debug_Q_32(reg32_2_debug_q_32), .CLK(Clock),
    .OE(T2OE), .Clear(CLR));
  // Probe on RegisterAddressBus
  assign InternalDataBus = C1OE ? 32'h1 : 32'bz;  // Controlled_Buffer controlled_buffer_6
  RAM #(.addrWidth(4), .dataWidth(32)) ram_1 (
    .addr(RegisterAddressBus), .data(InternalDataBus), .sel(RegSEL), .clk(Inverted_Clock), .ld(RegLD),
    .clr(CLR));
  // Probe on InternalDataBus
  assign RegisterAddressBus = PCOE ? 4'b1111 : 4'bz;  // Controlled_Buffer controlled_buffer_7
  assign Opr = AADD ? 4'b0001 : 4'bz;  // Controlled_Buffer controlled_buffer_8
  nor nor_1 (nor_1_out, InterconnectionAddressBus[6], InterconnectionAddressBus[7], InterconnectionAddressBus[8], InterconnectionAddressBus[9], InterconnectionAddressBus[10], InterconnectionAddressBus[11], InterconnectionAddressBus[12], InterconnectionAddressBus[13], InterconnectionAddressBus[14], InterconnectionAddressBus[15], InterconnectionAddressBus[16], InterconnectionAddressBus[17], InterconnectionAddressBus[18], InterconnectionAddressBus[19], InterconnectionAddressBus[20], InterconnectionAddressBus[21], InterconnectionAddressBus[22], InterconnectionAddressBus[23], InterconnectionAddressBus[24], InterconnectionAddressBus[25], InterconnectionAddressBus[26], InterconnectionAddressBus[27], InterconnectionAddressBus[28], InterconnectionAddressBus[29], InterconnectionAddressBus[30], InterconnectionAddressBus[31]);
  assign controlled_buffer_9_out = IBRead ? InterconnectionDataBus : 32'bz;  // Controlled_Buffer controlled_buffer_9
  assign controlled_buffer_9_out = MDRput ? InternalDataBus : 32'bz;  // Controlled_Buffer controlled_buffer_10
  and and_2 (and_2_out, nor_1_out, or_1_out);
  // Probe on reg32_3_debug_q_32
  // Probe on reg32_4_debug_q_32
  or or_1 (or_1_out, IBWrite, IBRead);
  assign InterconnectionDataBus = IBWrite ? reg32_3_dout_32 : 32'bz;  // Controlled_Buffer controlled_buffer_11
  Reg32 reg32_3 (
    .DIn_32(controlled_buffer_9_out), .CE(MDRCE), .DOut_32(reg32_3_dout_32), .Debug_Q_32(reg32_3_debug_q_32),
    .CLK(Clock), .OE(MDROE), .Clear(CLR));
  assign InternalDataBus = MDRget ? reg32_3_dout_32 : 32'bz;  // Controlled_Buffer controlled_buffer_12
  Reg32 reg32_4 (
    .DIn_32(InternalDataBus), .CE(MARCE), .DOut_32(InterconnectionAddressBus),
    .Debug_Q_32(reg32_4_debug_q_32), .CLK(Clock), .OE(MAROE), .Clear(CLR));
  RAM #(.addrWidth(6), .dataWidth(32)) ram_2 (
    .addr(InterconnectionAddressBus[5:0]), .data(InterconnectionDataBus), .sel(and_2_out),
    .clk(Inverted_Clock), .ld(IBRead));  // open: clr

  // Notes on the sheet:
  //   Decode ROM
  //   Use opcode to pick next state during decode state
  //   (Does not clear ROM contents)
  //   For each instruction, this ROM holds the next state that follows the Decode State.
  //   This design requies that Decode state is state  0x03
  //   contents of rom_1 (hex, n*v repeats v):
  //   0 4 4 5 4 4 4 5
  //   Control FSM
  //   upper 4 bits of opcode
  //   not used in this lab
  //   next state from Output ROM
  //   Control FSM Outputs
  //   (Poke to toggle)
  //   Invert for latching if needed
  //   contents of rom_2 (hex, n*v repeats v):
  //   24023801 1b100602 40c20003 20022107 2b805 47606 32100 7
  //   Register Address Bus
  //   16 x 32-bit Register Bank
  //   in Part 2 ONLY!
  //   Use this Main Memory component 
endmodule
